# Fritzing sketch sensor_node (saved by Fritzing 0.8.7b)
circuit board: 8.46667cm x 5.64444cm
breadboards: 1

parts:
  Part1 = Arduino Uno (Rev3)
  R1 = Photocell (LDR) [package=THT]
  R2 = Resistor [tolerance=±5% resistance=10k package=THT]
  DHT23 = Humidity and Temperature Sensor RHT03 [part_number=DHT11/DHT22]
  U1 = mystery part, 4 pins [chip_label=Buzzer part_number="5V DC Buzzer"]

nets:
  N1: Part1.A0, R1.pin_0, R2.Pin_0
  N2: Part1.D10_PWM/SS, U1.pin1
  N3: Part1.D3_PWM, DHT23.Data-signal
  5V: Part1.5V, R1.pin_1, DHT23.Vcc, U1.pin4
  N4: Part1.GND, R2.Pin_1, DHT23.GND_2
